# Fritzing sketch esquematico (saved by Fritzing 0.9.3b)
breadboards: 1

parts:
  Componente1 = Arduino Nano (Rev3.0)
  DHT1 = DHT11 Humitidy and Temperature Sensor
  Componente2 = MQ-3 breakout
  R1 = Resistor [tolerance=±5% resistance=10k package=THT]

nets:
  GND: Componente1.GND, DHT1.GND, Componente2.GND
  N1: Componente1.D5, DHT1.DATA, R1.Pin_0
  N2: Componente1.D6, Componente2.DO
  5V: Componente1.5V, DHT1.VDD, Componente2.VCC, R1.Pin_1

notes:
  MQ-2
  Alimentação (5V/1A) e programação
  ---------------------->

custom parts:
  DHT11 Humitidy and Temperature Sensor: DHT11 Humidity and Temperature Sensor
  MQ-3 breakout: Alcohol sensor is capable of detecting alcohol (ethanol) particles on itself and gives the information in digital form back to us to manipulate with it. SKU:101251 • Voltage: 5V DC • Power: max 750mW • Measurement range: 0.04-4mg/L
